# Fritzing sketch Breadboard Layout (saved by Fritzing 0.7.12b)
breadboards: 1

parts:
  U1 = atmega328 [package=dip]
  S1 = Pushbutton [package="[THT]"]
  S2 = Pushbutton [package="[THT]"]
  R1 = Resistor [tolerance=±5% resistance=220 package=THT]
  R2 = Resistor [tolerance=±5% resistance=220 package=THT]
  LED1 = RGB LED (com. anode, rbg) [package="5 mm [THT]"]
  VCC1 = Battery
  S3 = Pushbutton [package="[THT]"]
  Bauteil1 = Bluetooth Module Breakout - Roving Networks (RN-41)

nets:
  N1: U1.RESET, S3.Pin_1, S3.Pin_2
  N2: U1.D0_(RX), Bauteil1.UARTTX
  N3: U1.D1_(TX), Bauteil1.UARTRX
  N4: U1.D2, S1.Pin_3, S1.Pin_4, R2.Pin_1
  N5: U1.D3_(PWM), S2.Pin_3, S2.Pin_4, R1.Pin_1
  VCC: U1.VCC, R1.Pin_0, VCC1.+, Bauteil1.VCC
  N6: U1.GND#7, S2.Pin_1, S2.Pin_2, LED1.common_anode, VCC1.-, S3.Pin_3, S3.Pin_4, Bauteil1.GND
  N7: U1.D5_(PWM), LED1.red_cathode
  N8: U1.D6_(PWM), LED1.blue_cathode
  N9: S1.Pin_1, S1.Pin_2

notes:
  Button A
  Button B
  Progress LED
  Reset Button
  Bluetooth Modul
